# Fritzing sketch raspberry_pi_temp_sensor (saved by Fritzing 0.9.2b)
breadboards: 1

parts:
  Raspberry_Pi1 = Raspberry Pi 2
  IC1 = IC, DIP package, 8 pins [chip_label=MPC3002]
  T1 = LM35 Temperature Sensor [package="TO92 [THT]"]
  C1 = Ceramic Capacitor [capacitance=100nF package="100 mil [THT, multilayer]"]

nets:
  N1: Raspberry_Pi1.3v3, IC1.pin8, T1.+Vs, C1.0
  N2: Raspberry_Pi1.GIPO10, IC1.pin5
  N3: Raspberry_Pi1.GIPO9, IC1.pin6
  N4: Raspberry_Pi1.GIPO11, IC1.pin7
  GND: Raspberry_Pi1.GND, IC1.pin4, T1.GND, C1.1
  N5: IC1.pin2, T1.Vout
